# Fritzing sketch Alhambra-button-pull-down (saved by Fritzing 0.9.3b)
breadboards: 1

parts:
  Part1 = iceZUM Alhambra
  S3 = Momentary Switch [package=ksa_sealed_tac_switch]
  R1 = Resistor [tolerance=±5% resistance=4.7k package="0402 [SMD]"]

nets:
  N1: Part1.D0, Part1.V0#59, S3.3, R1.Pin_1
  N2: Part1.G0, R1.Pin_0
  N3: Part1.V0#45, S3.1

custom parts:
  iceZUM Alhambra: Arduino/zum compatible Open FPGA electronic board. Synthesize hardware easily, using only open source tools
