# Fritzing sketch button-direct-1 (saved by Fritzing 0.9.3b)
breadboards: 1

parts:
  Part1 = iceZUM Alhambra
  S3 = Momentary Switch [package=ksa_sealed_tac_switch]

nets:
  N1: Part1.D0, Part1.V0, S3.2
  N2: Part1.G0, S3.4

custom parts:
  iceZUM Alhambra: Arduino/zum compatible Open FPGA electronic board. Synthesize hardware easily, using only open source tools
