# Fritzing sketch interrupt-direct-1 (saved by Fritzing 0.9.3b)
breadboards: 1

parts:
  Part1 = iceZUM Alhambra
  U1 = SWITCH_SPDT [package=kps-1290]

nets:
  N1: Part1.D0, Part1.V0, U1.P
  N2: Part1.G0, U1.O

custom parts:
  iceZUM Alhambra: Arduino/zum compatible Open FPGA electronic board. Synthesize hardware easily, using only open source tools
