# Fritzing sketch microswitches-direct-1 (saved by Fritzing 0.9.3b)
breadboards: 1

parts:
  Part1 = iceZUM Alhambra
  SW1 = DIP Switch 8 Position [package=dipswitch-08]

nets:
  N1: Part1.D0, Part1.V0, SW1.16
  N2: Part1.G0, SW1.1

custom parts:
  iceZUM Alhambra: Arduino/zum compatible Open FPGA electronic board. Synthesize hardware easily, using only open source tools
