# Fritzing sketch Alhambra-led1-cables-hembra-hembra (saved by Fritzing 0.9.6b)

parts:
  Part1 = iceZUM Alhambra
  LED12 = LED - 3mm [color="Red (633nm)" current=0.030 package="3 mm [THT]"]

nets:
  N1: Part1.G0, LED12.anode
  N2: Part1.V0, LED12.cathode

custom parts:
  iceZUM Alhambra: Arduino/zum compatible Open FPGA electronic board. Synthesize hardware easily, using only open source tools
