# Fritzing sketch Alhambra-led8 (saved by Fritzing 0.9.6b)
breadboards: 1

parts:
  Part1 = iceZUM Alhambra
  LED12 = LED - 3mm [color="Red (633nm)" current=0.030 package="3 mm [THT]"]
  LED13 = LED - 3mm [color="Red (633nm)" current=0.030 package="3 mm [THT]"]
  LED14 = LED - 3mm [color="Red (633nm)" current=0.030 package="3 mm [THT]"]
  LED15 = LED - 3mm [color="Red (633nm)" current=0.030 package="3 mm [THT]"]
  LED16 = LED - 3mm [color="Red (633nm)" current=0.030 package="3 mm [THT]"]
  LED17 = LED - 3mm [color="Red (633nm)" current=0.030 package="3 mm [THT]"]
  LED18 = LED - 3mm [color="Red (633nm)" current=0.030 package="3 mm [THT]"]
  LED19 = LED - 3mm [color="Red (633nm)" current=0.030 package="3 mm [THT]"]

nets:
  N1: Part1.D7, Part1.V7, LED19.anode
  N2: Part1.G0, Part1.GA2, LED12.cathode, LED13.cathode, LED14.cathode, LED15.cathode, LED16.cathode, LED17.cathode, LED18.cathode, LED19.cathode
  N3: Part1.V6, LED18.anode
  N4: Part1.V5, LED17.anode
  N5: Part1.V4, LED16.anode
  N6: Part1.V3, LED15.anode
  N7: Part1.V2, LED14.anode
  N8: Part1.V1, LED13.anode
  N9: Part1.V0, LED12.anode

custom parts:
  iceZUM Alhambra: Arduino/zum compatible Open FPGA electronic board. Synthesize hardware easily, using only open source tools
