# Fritzing sketch LED2-protoboard (saved by Fritzing 0.9.6b)
breadboards: 1

parts:
  Part1 = iceZUM Alhambra
  LED12 = LED - 3mm [color="Red (633nm)" current=0.030 package="3 mm [THT]"]
  LED13 = LED - 3mm [color="Red (633nm)" current=0.030 package="3 mm [THT]"]

nets:
  N1: Part1.G0, LED12.anode, LED13.anode
  N2: Part1.V1, LED13.cathode
  N3: Part1.V0, LED12.cathode

custom parts:
  iceZUM Alhambra: Arduino/zum compatible Open FPGA electronic board. Synthesize hardware easily, using only open source tools
