# Fritzing sketch arduino-alhambra-1 (saved by Fritzing 0.9.3b)

parts:
  Part1 = iceZUM Alhambra
  Part2 = Arduino Uno (Rev3) - ICSP

nets:
  N1: Part1.D10, Part2.D10_PWM/SS
  N2: Part1.D11, Part2.D11_PWM/MOSI
  N3: Part1.D12, Part2.D12/MISO
  N4: Part1.D13, Part2.D13/SCK
  N5: Part1.G, Part1.G7, Part2.GND

custom parts:
  iceZUM Alhambra: Arduino/zum compatible Open FPGA electronic board. Synthesize hardware easily, using only open source tools
