# Fritzing sketch arduino-alhambra-2 (saved by Fritzing 0.9.3b)

parts:
  Part1 = iceZUM Alhambra
  Part2 = Arduino Uno (Rev3) - ICSP
  Part3 = iceZUM Alhambra

nets:
  N1: Part1.D10, Part2.D10_PWM/SS
  N2: Part1.D11, Part1.V11, Part2.D11_PWM/MOSI, Part3.V11
  N3: Part1.D12, Part1.V12, Part2.D12/MISO, Part3.V12
  N4: Part1.D13, Part1.V13, Part2.D13/SCK, Part3.V13
  N5: Part1.G, Part1.G7, Part2.GND
  N6: Part1.VD5, Part3.VD0
  N7: Part1.GD5, Part3.GD0
  N8: Part2.D9_PWM, Part3.D10

custom parts:
  iceZUM Alhambra: Arduino/zum compatible Open FPGA electronic board. Synthesize hardware easily, using only open source tools
