# Fritzing sketch cap1188-alhambra-ii (saved by Fritzing 0.9.3b)
breadboards: 1

parts:
  Part1 = iceZUM Alhambra
  Part2 = Adafruit CAP1188 - 8-Key Capacitive Touch Sensor Breakout [part_number="Adafruit #1602"]

nets:
  N1: Part1.G13, Part1.G12, Part1.G11, Part1.G10, Part2.WAKE/MOSI, Part2.CS, Part2.SDA/MISO, Part2.SCK
  N2: Part1.5VP, Part2.VIN
  GND: Part1.GND, Part2.RESET, Part2.ADDR, Part2.GND

custom parts:
  iceZUM Alhambra: Arduino/zum compatible Open FPGA electronic board. Synthesize hardware easily, using only open source tools
  Adafruit CAP1188 - 8-Key Capacitive Touch Sensor Breakout: Add lots of touch sensors to your next microcontroller project with this easy-to-use 8-channel capacitive touch sensor breakout board, starring the CAP1188. This chip can handle up to 8 individual touch pads, and has a very nice feature that makes it stand out for us: it will light up the 8 onboard LEDs when the matching touch sensor fires to help you debug your sensor setup. The CAP1188 has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
