# Fritzing sketch display-alhambra (saved by Fritzing 0.9.3b)

parts:
  Part1 = iceZUM Alhambra
  SparkFun_7-Segment-Display-Yellow1 = SparkFun 7-Segment Serial Display-Red [part_number=COM-11441]

nets:
  N1: Part1.V13, SparkFun_7-Segment-Display-Yellow1.SCK
  N2: Part1.V11, SparkFun_7-Segment-Display-Yellow1.MOSI
  N3: Part1.V10, SparkFun_7-Segment-Display-Yellow1.!SS
  N4: Part1.VD2, Part1.VD5, SparkFun_7-Segment-Display-Yellow1.VCC
  N5: Part1.GD5, SparkFun_7-Segment-Display-Yellow1.GND

custom parts:
  iceZUM Alhambra: Arduino/zum compatible Open FPGA electronic board. Synthesize hardware easily, using only open source tools
  SparkFun 7-Segment Serial Display-Red: Description: 4-digit 7-segment displays are really neat little devices, it’s a shame that they can be so cumbersome to control. Well we’ve solved that problem by making them a little bit “smarter.” The SparkFun 7-Segment Serial Display combines a classic 4-digit 7-segment display and an ATMega328 microcontroller allowing you to control every segment individually using only a few serial lines.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
